// Logisim project satanja.circ as structural Verilog: 7 circuits, main circuit CPU
module CPU (
  input  [7:0] in_1,
  input  ManualBC,
  input  ManualCSC,
  input  LO,
  input  AI,
  input  CI,
  input  OI,
  input  PW,
  input  PO,
  input  DI,
  input  MO,
  input  MI,
  input  PE,
  input  II,
  input  HLT,
  input  AO,
  input  CO
);

  wire AI_t, and_2_out, AO_t, CI_t, CLK, clock_1_out, CO_t, DI_t, HLT_t, II_t, LO_t, MI_t, MO_t, not_1_out,
       not_2_out, not_3_out, not_4_out, OI_t, or_1_out, PE_t, PO_t, PW_t;
  wire [3:0] alu_1_fv, Flags, OCReg_q;
  wire [7:0] Acc_q, alu_1_o, and_1_out, AReg_q, Busse, InstructionCountre_o, IR_q, MAR_q, ProgramCountre_o,
       ram_1_dout, rom_1_data, rom_2_data, xor_1_out;
  wire [7:7] nor_1_out;

  not not_1 (not_1_out, CLK);
  assign and_1_out = {8{1'b0}} & {8{nor_1_out[7]}};  // AND_Gate and_1, 8 bits wide
  not not_2 (not_2_out, nor_1_out[7]);
  Register IR (.D(Busse), .en(II_t), .clk(CLK), .Q(IR_q));  // open: clr
  // Probe on InstructionCountre_o
  nor nor_1 (nor_1_out[7], xor_1_out[0], xor_1_out[1], xor_1_out[2], xor_1_out[3], xor_1_out[4], xor_1_out[5], xor_1_out[6], xor_1_out[7]);
  Countre InstructionCountre (.I(and_1_out), .Ew(not_2_out), .c(not_1_out), .O(InstructionCountre_o));  // open: co
  Register MAR (.D(Busse), .en(DI_t), .clk(CLK), .Q(MAR_q), .clr(1'b0));
  ROM #(.addrWidth(15)) rom_1 (.addr({IR_q, Flags, InstructionCountre_o[2:0]}), .data(rom_1_data));
  assign xor_1_out = InstructionCountre_o ^ 8'h8;  // XOR_Gate xor_1, 8 bits wide
  ROM #(.addrWidth(15)) rom_2 (.addr({IR_q, Flags, InstructionCountre_o[2:0]}), .data(rom_2_data));
  RAM #(.enables("line")) ram_1 (.addr(MAR_q), .we(MI_t), .clk(CLK), .din(Busse), .dout(ram_1_dout));
  not not_3 (not_3_out, ManualCSC);
  assign LO_t = not_3_out ? rom_1_data[0] : 1'bz;  // Controlled_Buffer controlled_buffer_1
  assign AI_t = not_3_out ? rom_1_data[1] : 1'bz;  // Controlled_Buffer controlled_buffer_2
  assign CI_t = not_3_out ? rom_1_data[2] : 1'bz;  // Controlled_Buffer controlled_buffer_3
  assign OI_t = not_3_out ? rom_1_data[3] : 1'bz;  // Controlled_Buffer controlled_buffer_4
  assign PW_t = not_3_out ? rom_1_data[4] : 1'bz;  // Controlled_Buffer controlled_buffer_5
  assign PO_t = not_3_out ? rom_1_data[5] : 1'bz;  // Controlled_Buffer controlled_buffer_6
  assign DI_t = not_3_out ? rom_1_data[6] : 1'bz;  // Controlled_Buffer controlled_buffer_7
  assign MO_t = not_3_out ? rom_1_data[7] : 1'bz;  // Controlled_Buffer controlled_buffer_8
  assign MI_t = not_3_out ? rom_2_data[0] : 1'bz;  // Controlled_Buffer controlled_buffer_9
  assign PE_t = not_3_out ? rom_2_data[1] : 1'bz;  // Controlled_Buffer controlled_buffer_10
  assign II_t = not_3_out ? rom_2_data[2] : 1'bz;  // Controlled_Buffer controlled_buffer_11
  assign HLT_t = not_3_out ? rom_2_data[3] : 1'bz;  // Controlled_Buffer controlled_buffer_12
  assign AO_t = not_3_out ? rom_2_data[4] : 1'bz;  // Controlled_Buffer controlled_buffer_13
  assign CO_t = not_3_out ? rom_2_data[5] : 1'bz;  // Controlled_Buffer controlled_buffer_14
  Controlled_Buffer controlled_buffer_15 (.in(rom_2_data[6]), .en(not_3_out));  // open: out
  Controlled_Buffer controlled_buffer_16 (.in(rom_2_data[7]), .en(not_3_out));  // open: out
  assign Busse = ManualBC ? in_1 : 8'bz;  // Controlled_Buffer controlled_buffer_17
  assign Busse = MO_t ? ram_1_dout : 8'bz;  // Controlled_Buffer controlled_buffer_18
  // Probe on Busse
  or or_1 (or_1_out, PE_t, PW_t);
  Register AReg (.D(Busse), .en(AI_t), .clk(CLK), .Q(AReg_q), .clr(1'b0));
  Register Acc (.D(Busse), .en(CI_t), .clk(CLK), .Q(Acc_q), .clr(1'b0));
  Register #(.width(4)) OCReg (.D(Busse[3:0]), .en(OI_t), .clk(CLK), .Q(OCReg_q), .clr(1'b0));
  not not_4 (not_4_out, PW_t);
  and and_2 (and_2_out, CLK, or_1_out);
  assign Busse = AO_t ? AReg_q : 8'bz;  // Controlled_Buffer controlled_buffer_19
  assign Busse = CO_t ? Acc_q : 8'bz;  // Controlled_Buffer controlled_buffer_20
  // Probe on ProgramCountre_o
  Countre ProgramCountre (.I(Busse), .Ew(not_4_out), .c(and_2_out), .O(ProgramCountre_o));  // open: co
  ALU alu_1 (
    .A(AReg_q), .B(Acc_q), .Oc(OCReg_q), .O(alu_1_o), .Fv(alu_1_fv[0]), .Fc(alu_1_fv[1]), .Fs(alu_1_fv[2]),
    .Fz(alu_1_fv[3]));
  Clock clock_1 (.out(clock_1_out));
  assign LO_t = ManualCSC ? LO : 1'bz;  // Controlled_Buffer controlled_buffer_21
  assign AI_t = ManualCSC ? AI : 1'bz;  // Controlled_Buffer controlled_buffer_22
  assign CI_t = ManualCSC ? CI : 1'bz;  // Controlled_Buffer controlled_buffer_23
  assign OI_t = ManualCSC ? OI : 1'bz;  // Controlled_Buffer controlled_buffer_24
  assign PW_t = ManualCSC ? PW : 1'bz;  // Controlled_Buffer controlled_buffer_25
  assign PO_t = ManualCSC ? PO : 1'bz;  // Controlled_Buffer controlled_buffer_26
  assign DI_t = ManualCSC ? DI : 1'bz;  // Controlled_Buffer controlled_buffer_27
  assign MO_t = ManualCSC ? MO : 1'bz;  // Controlled_Buffer controlled_buffer_28
  assign MI_t = ManualCSC ? MI : 1'bz;  // Controlled_Buffer controlled_buffer_29
  assign PE_t = ManualCSC ? PE : 1'bz;  // Controlled_Buffer controlled_buffer_30
  assign II_t = ManualCSC ? II : 1'bz;  // Controlled_Buffer controlled_buffer_31
  assign HLT_t = ManualCSC ? HLT : 1'bz;  // Controlled_Buffer controlled_buffer_32
  assign AO_t = ManualCSC ? AO : 1'bz;  // Controlled_Buffer controlled_buffer_33
  assign CO_t = ManualCSC ? CO : 1'bz;  // Controlled_Buffer controlled_buffer_34
  assign Busse = PO_t ? ProgramCountre_o : 8'bz;  // Controlled_Buffer controlled_buffer_35
  assign Busse = LO_t ? alu_1_o : 8'bz;  // Controlled_Buffer controlled_buffer_36
  and and_3 (CLK, clock_1_out, ~HLT_t);  // AND_Gate
  Register #(.width(4)) FlagRegister (.D(alu_1_fv), .en(LO_t), .clk(CLK), .Q(Flags));  // open: clr

  // Notes on the sheet:
  //   contents of rom_1 (hex, n*v repeats v):
  //   60 80 6*0 60 80 6*0 60 80 6*0 60 80 6*0 60 80 6*0 60 80 6*0 60 80 6*0 60 80 6*0 60 80 6*0 60 80 6*0
  //   60 80 6*0 60 80 6*0 60 80 6*0 60 80 6*0 60 80 6*0 60 80 6*0 60 80 0 60 82 0 0 0 60 80 0 60 82 0 0 0
  //   60 80 0 60 82 0 0 0 60 80 0 60 82 0 0 0 60 80 0 60 82 0 0 0 60 80 0 60 82 0 0 0 60 80 0 60 82 0 0 0
  //   60 80 0 60 82 0 0 0 60 80 0 60 82 0 0 0 60 80 0 60 82 0 0 0 60 80 0 60 82 0 0 0 60 80 0 60 82 0 0 0
  //   60 80 0 60 82 0 0 0 60 80 0 60 82 0 0 0 60 80 0 60 82 0 0 0 60 80 0 60 82 0 0 0 60 80 0 60 c0 0 0 0
  //   60 80 0 60 c0 0 0 0 60 80 0 60 c0 0 0 0 60 80 0 60 c0 0 0 0 60 80 0 60 c0 0 0 0 60 80 0 60 c0 0 0 0
  //   60 80 0 60 c0 0 0 0 60 80 0 60 c0 0 0 0 60 80 0 60 c0 0 0 0 60 80 0 60 c0 0 0 0 60 80 0 60 c0 0 0 0
  //   60 80 0 60 c0 0 0 0 60 80 0 60 c0 0 0 0 60 80 0 60 c0 0 0 0 60 80 0 60 c0 0 0 0 60 80 0 60 c0 0 0 0
  //   60 80 0 60 c0 82 0 0 60 80 0 60 c0 82 0 0 60 80 0 60 c0 82 0 0 60 80 0 60 c0 82 0 0 60 80 0 60 c0 82
  //   0 0 60 80 0 60 c0 82 0 0 60 80 0 60 c0 82 0 0 60 80 0 60 c0 82 0 0 60 80 0 60 c0 82 0 0 60 80 0 60
  //   c0 82 0 0 60 80 0 60 c0 82 0 0 60 80 0 60 c0 82 0 0 60 80 0 60 c0 82 0 0 60 80 0 60 c0 82 0 0 60 80
  //   0 60 c0 82 0 0 60 80 0 60 c0 82 0 0 60 80 0 60 c0 0 0 0 60 80 0 60 c0 0 0 0 60 80 0 60 c0 0 0 0 60
  //   80 0 60 c0 0 0 0 60 80 0 60 c0 0 0 0 60 80 0 60 c0 0 0 0 60 80 0 60 c0 0 0 0 60 80 0 60 c0 0 0 0 60
  //   80 0 60 c0 0 0 0 60 80 0 60 c0 0 0 0 60 80 0 60 c0 0 0 0 60 80 0 60 c0 0 0 0 60 80 0 60 c0 0 0 0 60
  //   80 0 60 c0 0 0 0 60 80 0 60 c0 0 0 0 60 80 0 60 c0 0 0 0 60 80 0 60 c0 84 0 0 60 80 0 60 c0 84 0 0
  //   60 80 0 60 c0 84 0 0 60 80 0 60 c0 84 0 0 60 80 0 60 c0 84 0 0 60 80 0 60 c0 84 0 0 60 80 0 60 c0 84
  //   0 0 60 80 0 60 c0 84 0 0 60 80 0 60 c0 84 0 0 60 80 0 60 c0 84 0 0 60 80 0 60 c0 84 0 0 60 80 0 60
  //   c0 84 0 0 60 80 0 60 c0 84 0 0 60 80 0 60 c0 84 0 0 60 80 0 60 c0 84 0 0 60 80 0 60 c0 84 0 0 60 80
  //   0 60 88 0 0 0 60 80 0 60 88 0 0 0 60 80 0 60 88 0 0 0 60 80 0 60 88 0 0 0 60 80 0 60 88 0 0 0 60 80
  //   0 60 88 0 0 0 60 80 0 60 88 0 0 0 60 80 0 60 88 0 0 0 60 80 0 60 88 0 0 0 60 80 0 60 88 0 0 0 60 80
  //   0 60 88 0 0 0 60 80 0 60 88 0 0 0 60 80 0 60 88 0 0 0 60 80 0 60 88 0 0 0 60 80 0 60 88 0 0 0 60 80
  //   0 60 88 0 0 0 60 80 0 60 c0 84 5 0 60 80 0 60 c0 84 5 0 60 80 0 60 c0 84 5 0 60 80 0 60 c0 84 5 0 60
  //   80 0 60 c0 84 5 0 60 80 0 60 c0 84 5 0 60 80 0 60 c0 84 5 0 60 80 0 60 c0 84 5 0 60 80 0 60 c0 84 5
  //   0 60 80 0 60 c0 84 5 0 60 80 0 60 c0 84 5 0 60 80 0 60 c0 84 5 0 60 80 0 60 c0 84 5 0 60 80 0 60 c0
  //   84 5 0 60 80 0 60 c0 84 5 0 60 80 0 60 c0 84 5 31617*0 60 80 6*0 60 80 6*0 60 80 6*0 60 80 6*0 60 80
  //   6*0 60 80 6*0 60 80 6*0 60 80 6*0 60 80 6*0 60 80 6*0 60 80 6*0 60 80 6*0 60 80 6*0 60 80 6*0 60 80
  //   6*0 60 80
  //   contents of rom_2 (hex, n*v repeats v):
  //   0 4 2 6*0 4 2 6*0 4 2 6*0 4 2 6*0 4 2 6*0 4 2 6*0 4 2 6*0 4 2 6*0 4 2 6*0 4 2 6*0 4 2 6*0 4 2 6*0 4
  //   2 6*0 4 2 6*0 4 2 6*0 4 2 6*0 4 2 0 2 4*0 4 2 0 2 4*0 4 2 0 2 4*0 4 2 0 2 4*0 4 2 0 2 4*0 4 2 0 2
  //   4*0 4 2 0 2 4*0 4 2 0 2 4*0 4 2 0 2 4*0 4 2 0 2 4*0 4 2 0 2 4*0 4 2 0 2 4*0 4 2 0 2 4*0 4 2 0 2 4*0
  //   4 2 0 2 4*0 4 2 0 2 4*0 4 2 0 0 13 0 0 0 4 2 0 0 13 0 0 0 4 2 0 0 13 0 0 0 4 2 0 0 13 0 0 0 4 2 0 0
  //   13 0 0 0 4 2 0 0 13 0 0 0 4 2 0 0 13 0 0 0 4 2 0 0 13 0 0 0 4 2 0 0 13 0 0 0 4 2 0 0 13 0 0 0 4 2 0
  //   0 13 0 0 0 4 2 0 0 13 0 0 0 4 2 0 0 13 0 0 0 4 2 0 0 13 0 0 0 4 2 0 0 13 0 0 0 4 2 0 0 13 0 0 0 4 2
  //   0 0 2 0 0 0 4 2 0 0 2 0 0 0 4 2 0 0 2 0 0 0 4 2 0 0 2 0 0 0 4 2 0 0 2 0 0 0 4 2 0 0 2 0 0 0 4 2 0 0
  //   2 0 0 0 4 2 0 0 2 0 0 0 4 2 0 0 2 0 0 0 4 2 0 0 2 0 0 0 4 2 0 0 2 0 0 0 4 2 0 0 2 0 0 0 4 2 0 0 2 0
  //   0 0 4 2 0 0 2 0 0 0 4 2 0 0 2 0 0 0 4 2 0 0 2 0 0 0 4 2 0 0 23 0 0 0 4 2 0 0 23 0 0 0 4 2 0 0 23 0 0
  //   0 4 2 0 0 23 0 0 0 4 2 0 0 23 0 0 0 4 2 0 0 23 0 0 0 4 2 0 0 23 0 0 0 4 2 0 0 23 0 0 0 4 2 0 0 23 0
  //   0 0 4 2 0 0 23 0 0 0 4 2 0 0 23 0 0 0 4 2 0 0 23 0 0 0 4 2 0 0 23 0 0 0 4 2 0 0 23 0 0 0 4 2 0 0 23
  //   0 0 0 4 2 0 0 23 0 0 0 4 2 0 0 2 0 0 0 4 2 0 0 2 0 0 0 4 2 0 0 2 0 0 0 4 2 0 0 2 0 0 0 4 2 0 0 2 0 0
  //   0 4 2 0 0 2 0 0 0 4 2 0 0 2 0 0 0 4 2 0 0 2 0 0 0 4 2 0 0 2 0 0 0 4 2 0 0 2 0 0 0 4 2 0 0 2 0 0 0 4
  //   2 0 0 2 0 0 0 4 2 0 0 2 0 0 0 4 2 0 0 2 0 0 0 4 2 0 0 2 0 0 0 4 2 0 0 2 0 0 0 4 2 0 2 4*0 4 2 0 2
  //   4*0 4 2 0 2 4*0 4 2 0 2 4*0 4 2 0 2 4*0 4 2 0 2 4*0 4 2 0 2 4*0 4 2 0 2 4*0 4 2 0 2 4*0 4 2 0 2 4*0
  //   4 2 0 2 4*0 4 2 0 2 4*0 4 2 0 2 4*0 4 2 0 2 4*0 4 2 0 2 4*0 4 2 0 2 4*0 4 2 0 0 0 2 0 0 4 2 0 0 0 2
  //   0 0 4 2 0 0 0 2 0 0 4 2 0 0 0 2 0 0 4 2 0 0 0 2 0 0 4 2 0 0 0 2 0 0 4 2 0 0 0 2 0 0 4 2 0 0 0 2 0 0
  //   4 2 0 0 0 2 0 0 4 2 0 0 0 2 0 0 4 2 0 0 0 2 0 0 4 2 0 0 0 2 0 0 4 2 0 0 0 2 0 0 4 2 0 0 0 2 0 0 4 2
  //   0 0 0 2 0 0 4 2 0 0 0 2 31618*0 4 2 8 5*0 4 2 8 5*0 4 2 8 5*0 4 2 8 5*0 4 2 8 5*0 4 2 8 5*0 4 2 8
  //   5*0 4 2 8 5*0 4 2 8 5*0 4 2 8 5*0 4 2 8 5*0 4 2 8 5*0 4 2 8 5*0 4 2 8 5*0 4 2 8 5*0 4 2 8
endmodule

module ALU (
  input  [7:0] A,
  input  [7:0] B,
  input  [3:0] Oc,
  output [7:0] O,
  output Fv,
  output Fc,
  output Fs,
  output Fz
);

  wire opcodetoflags_1_be, opcodetoflags_1_ci, opcodetoflags_1_e, opcodetoflags_1_ia, opcodetoflags_1_ib,
       opcodetoflags_1_io, opcodetoflags_1_l, opcodetoflags_1_n, opcodetoflags_1_r, opcodetoflags_1_x,
       shiftre_1_o_l, shiftre_1_o_r;
  wire [7:0] arithmeticlogic_1_o;

  OpCodeToFlags opcodetoflags_1 (
    .Oc(Oc), .Ia(opcodetoflags_1_ia), .Ib(opcodetoflags_1_ib), .Io(opcodetoflags_1_io),
    .Be(opcodetoflags_1_be), .N(opcodetoflags_1_n), .X(opcodetoflags_1_x), .Ci(opcodetoflags_1_ci),
    .E(opcodetoflags_1_e), .R(opcodetoflags_1_r), .L(opcodetoflags_1_l));
  ArithmeticLogic arithmeticlogic_1 (
    .A(A), .Ia(opcodetoflags_1_ia), .B(B), .Io(opcodetoflags_1_io), .Be(opcodetoflags_1_be),
    .Ib(opcodetoflags_1_ib), .N(opcodetoflags_1_n), .X(opcodetoflags_1_x), .Ci(opcodetoflags_1_ci),
    .O(arithmeticlogic_1_o), .Co(Fc));
  Shiftre shiftre_1 (
    .I(arithmeticlogic_1_o), .E(opcodetoflags_1_e), .R(opcodetoflags_1_r), .L(opcodetoflags_1_l),
    .O_r(shiftre_1_o_r), .O({O[7:1], Fs}), .O_l(shiftre_1_o_l));
  or or_1 (Fv, shiftre_1_o_r, shiftre_1_o_l);
  nor nor_1 (Fz, Fs, O[1], O[2], O[3], O[4], O[5], O[6], O[7]);

  assign O[0] = Fs;
endmodule

module ArithmeticLogic (
  input  [7:0] A,
  input  Ia,
  input  [7:0] B,
  input  Io,
  input  Be,
  input  Ib,
  input  N,
  input  X,
  input  Ci,
  output [7:0] O,
  output Co
);

  wire arithmeticlogicbit_2_co, arithmeticlogicbit_3_co, arithmeticlogicbit_4_co, arithmeticlogicbit_5_co,
       arithmeticlogicbit_6_co, arithmeticlogicbit_7_co, arithmeticlogicbit_8_co;
  wire [7:0] and_1_out, and_2_out, arithmeticlogicbit_8_o, or_1_out, xor_1_out;

  assign xor_1_out = A ^ {8{Ia}};  // XOR_Gate xor_1, 8 bits wide
  assign and_1_out = B & {8{Be}};  // AND_Gate and_1, 8 bits wide
  assign or_1_out = and_1_out | and_2_out;  // OR_Gate or_1, 8 bits wide
  assign and_2_out = ~B & {8{Ib}};  // AND_Gate and_2, 8 bits wide
  ArithmeticLogicBit arithmeticlogicbit_1 (
    .A(xor_1_out[7]), .B(or_1_out[7]), .Ci(arithmeticlogicbit_2_co), .N(N), .X(X), .Co(Co),
    .O(arithmeticlogicbit_8_o[7]));
  ArithmeticLogicBit arithmeticlogicbit_2 (
    .A(xor_1_out[6]), .B(or_1_out[6]), .Ci(arithmeticlogicbit_3_co), .N(N), .X(X),
    .Co(arithmeticlogicbit_2_co), .O(arithmeticlogicbit_8_o[6]));
  ArithmeticLogicBit arithmeticlogicbit_3 (
    .A(xor_1_out[5]), .B(or_1_out[5]), .Ci(arithmeticlogicbit_4_co), .N(N), .X(X),
    .Co(arithmeticlogicbit_3_co), .O(arithmeticlogicbit_8_o[5]));
  ArithmeticLogicBit arithmeticlogicbit_4 (
    .A(xor_1_out[4]), .B(or_1_out[4]), .Ci(arithmeticlogicbit_5_co), .N(N), .X(X),
    .Co(arithmeticlogicbit_4_co), .O(arithmeticlogicbit_8_o[4]));
  ArithmeticLogicBit arithmeticlogicbit_5 (
    .A(xor_1_out[3]), .B(or_1_out[3]), .Ci(arithmeticlogicbit_6_co), .N(N), .X(X),
    .Co(arithmeticlogicbit_5_co), .O(arithmeticlogicbit_8_o[3]));
  ArithmeticLogicBit arithmeticlogicbit_6 (
    .A(xor_1_out[2]), .B(or_1_out[2]), .Ci(arithmeticlogicbit_7_co), .N(N), .X(X),
    .Co(arithmeticlogicbit_6_co), .O(arithmeticlogicbit_8_o[2]));
  ArithmeticLogicBit arithmeticlogicbit_7 (
    .A(xor_1_out[1]), .B(or_1_out[1]), .Ci(arithmeticlogicbit_8_co), .N(N), .X(X),
    .Co(arithmeticlogicbit_7_co), .O(arithmeticlogicbit_8_o[1]));
  ArithmeticLogicBit arithmeticlogicbit_8 (
    .A(xor_1_out[0]), .B(or_1_out[0]), .Ci(Ci), .N(N), .X(X), .Co(arithmeticlogicbit_8_co),
    .O(arithmeticlogicbit_8_o[0]));
  assign O = {8{Io}} ^ arithmeticlogicbit_8_o;  // XOR_Gate xor_2, 8 bits wide
endmodule

module ArithmeticLogicBit (
  input  A,
  input  B,
  input  Ci,
  input  N,
  input  X,
  output Co,
  output O
);

  wire and_1_out, and_2_out, and_3_out, and_4_out, and_5_out, and_6_out, and_7_out, xor_1_out, xor_2_out;

  and and_1 (and_1_out, A, B);
  xor xor_1 (xor_1_out, A, B);
  and and_2 (and_2_out, and_1_out, N, ~X);  // AND_Gate
  and and_3 (and_3_out, and_1_out, ~N, ~X);  // AND_Gate
  and and_4 (and_4_out, xor_1_out, ~N, X);  // AND_Gate
  and and_5 (and_5_out, xor_1_out, ~N, ~X);  // AND_Gate
  and and_6 (and_6_out, Ci, ~N, ~X);  // AND_Gate
  and and_7 (and_7_out, and_6_out, and_5_out);
  xor xor_2 (xor_2_out, and_6_out, and_5_out);
  or or_1 (Co, and_3_out, and_7_out);
  or or_2 (O, and_2_out, and_4_out, xor_2_out);
endmodule

module Shiftre (
  input  [7:0] I,
  input  E,
  input  R,
  input  L,
  output O_r,
  output [7:0] O,
  output O_l
);

  wire and_1_out, and_2_out, and_4_out, and_5_out, and_6_out, and_7_out, and_8_out, and_9_out, and_10_out,
       and_11_out, and_12_out, and_13_out, and_14_out, and_15_out, and_16_out, and_17_out, and_18_out,
       and_19_out, and_20_out, and_21_out, and_22_out, and_23_out, and_24_out, and_25_out, and_26_out,
       not_1_out;

  not not_1 (not_1_out, E);
  and and_1 (and_1_out, E, ~R);  // AND_Gate
  and and_2 (and_2_out, E, R);
  and and_3 (O_r, I[0], and_2_out);
  and and_4 (and_4_out, I[0], not_1_out);
  and and_5 (and_5_out, I[0], and_1_out);
  and and_6 (and_6_out, I[1], and_2_out);
  and and_7 (and_7_out, I[1], not_1_out);
  and and_8 (and_8_out, I[1], and_1_out);
  and and_9 (and_9_out, I[2], and_2_out);
  and and_10 (and_10_out, I[2], not_1_out);
  and and_11 (and_11_out, I[2], and_1_out);
  and and_12 (and_12_out, I[3], and_2_out);
  and and_13 (and_13_out, I[3], not_1_out);
  and and_14 (and_14_out, I[3], and_1_out);
  and and_15 (and_15_out, I[4], and_2_out);
  and and_16 (and_16_out, I[4], not_1_out);
  and and_17 (and_17_out, I[4], and_1_out);
  and and_18 (and_18_out, I[5], and_2_out);
  and and_19 (and_19_out, I[5], not_1_out);
  and and_20 (and_20_out, I[5], and_1_out);
  and and_21 (and_21_out, I[6], and_2_out);
  and and_22 (and_22_out, I[6], not_1_out);
  and and_23 (and_23_out, I[6], and_1_out);
  and and_24 (and_24_out, I[7], and_2_out);
  and and_25 (and_25_out, I[7], not_1_out);
  and and_26 (and_26_out, I[7], R, L);
  and and_27 (O_l, I[7], and_1_out);
  or or_1 (O[0], and_4_out, and_6_out);
  or or_2 (O[1], and_5_out, and_7_out, and_9_out);
  or or_3 (O[2], and_8_out, and_10_out, and_12_out);
  or or_4 (O[3], and_11_out, and_13_out, and_15_out);
  or or_5 (O[4], and_14_out, and_16_out, and_18_out);
  or or_6 (O[5], and_17_out, and_19_out, and_21_out);
  or or_7 (O[6], and_20_out, and_22_out, and_24_out);
  or or_8 (O[7], and_23_out, and_25_out, and_26_out);
endmodule

module OpCodeToFlags (
  input  [3:0] Oc,
  output Ia,
  output Ib,
  output Io,
  output Be,
  output N,
  output X,
  output Ci,
  output E,
  output R,
  output L
);

  wire and_1_out, and_2_out, and_3_out, and_4_out, and_5_out, and_6_out, and_7_out, and_8_out, and_9_out,
       and_10_out, and_11_out, and_12_out, and_14_out, and_15_out, and_16_out, and_17_out, and_18_out,
       not_1_out, not_2_out, not_3_out, not_4_out;

  not not_1 (not_1_out, Oc[3]);
  not not_2 (not_2_out, Oc[2]);
  not not_3 (not_3_out, Oc[1]);
  not not_4 (not_4_out, Oc[0]);
  and and_1 (and_1_out, not_1_out, not_2_out, not_3_out, Oc[0]);
  and and_2 (and_2_out, not_1_out, not_2_out, Oc[1], not_4_out);
  and and_3 (and_3_out, Oc[3], Oc[2], not_3_out);
  and and_4 (and_4_out, not_1_out, Oc[2], Oc[0]);
  and and_5 (and_5_out, Oc[3], Oc[2], not_3_out);
  and and_6 (and_6_out, Oc[3], not_2_out, Oc[0]);
  and and_7 (and_7_out, Oc[3], Oc[2], not_3_out, not_4_out);
  and and_8 (and_8_out, not_1_out, Oc[2], not_3_out, Oc[0]);
  and and_9 (and_9_out, not_1_out, Oc[2], Oc[1], not_4_out);
  and and_10 (and_10_out, Oc[3], not_2_out);
  and and_11 (and_11_out, Oc[3], Oc[2]);
  and and_12 (and_12_out, not_2_out, Oc[1]);
  and and_13 (X, not_2_out, not_3_out);
  and and_14 (and_14_out, not_1_out, not_2_out, Oc[1], not_4_out);
  and and_15 (and_15_out, not_1_out, Oc[2], not_3_out, not_4_out);
  and and_16 (and_16_out, not_1_out, Oc[2], Oc[1], Oc[0]);
  and and_17 (and_17_out, not_1_out, not_2_out, Oc[1], Oc[0]);
  and and_18 (and_18_out, Oc[3], Oc[2], Oc[1]);
  or or_1 (Ia, and_1_out, and_2_out, and_3_out);
  or or_2 (Ib, and_4_out, and_5_out);
  or or_3 (Io, and_6_out, and_7_out);
  or or_4 (Be, and_8_out, and_9_out, and_10_out);
  or or_5 (N, and_11_out, and_12_out);
  or or_6 (Ci, and_14_out, and_15_out, and_16_out);
  or or_7 (E, and_17_out, and_18_out);

  assign L = Oc[0];
  assign R = Oc[2];
endmodule

module Countre (
  input  [7:0] I,
  input  Ew,
  input  c,
  output [7:0] O,
  output co
);

  wire t_ff_1_qn, t_ff_2_qn, t_ff_3_qn, t_ff_4_qn, t_ff_5_qn, t_ff_6_qn, t_ff_7_qn;
  wire [7:0] and_2_out, and_3_out, not_1_out;
  wire [7:7] and_1_out;

  and and_1 (and_1_out[7], ~Ew, c);  // AND_Gate
  assign and_2_out = I & {8{and_1_out[7]}};  // AND_Gate and_2, 8 bits wide
  assign not_1_out = ~I;  // NOT_Gate not_1, 8 bits wide
  assign and_3_out = not_1_out & {8{and_1_out[7]}};  // AND_Gate and_3, 8 bits wide
  T_Flip_Flop t_ff_1 (.T(Ew), .clk(c), .Q(O[0]), .Qn(t_ff_1_qn), .reset(and_3_out[0]), .preset(and_2_out[0]));
  T_Flip_Flop t_ff_2 (.T(Ew), .clk(t_ff_1_qn), .Q(O[1]), .Qn(t_ff_2_qn), .reset(and_3_out[1]), .preset(and_2_out[1]));
  T_Flip_Flop t_ff_3 (.T(Ew), .clk(t_ff_2_qn), .Q(O[2]), .Qn(t_ff_3_qn), .reset(and_3_out[2]), .preset(and_2_out[2]));
  T_Flip_Flop t_ff_4 (.T(Ew), .clk(t_ff_3_qn), .Q(O[3]), .Qn(t_ff_4_qn), .reset(and_3_out[3]), .preset(and_2_out[3]));
  T_Flip_Flop t_ff_5 (.T(Ew), .clk(t_ff_4_qn), .Q(O[4]), .Qn(t_ff_5_qn), .reset(and_3_out[4]), .preset(and_2_out[4]));
  T_Flip_Flop t_ff_6 (.T(Ew), .clk(t_ff_5_qn), .Q(O[5]), .Qn(t_ff_6_qn), .reset(and_3_out[5]), .preset(and_2_out[5]));
  T_Flip_Flop t_ff_7 (.T(Ew), .clk(t_ff_6_qn), .Q(O[6]), .Qn(t_ff_7_qn), .reset(and_3_out[6]), .preset(and_2_out[6]));
  T_Flip_Flop t_ff_8 (.T(Ew), .clk(t_ff_7_qn), .Q(O[7]), .Qn(co), .reset(and_3_out[7]), .preset(and_2_out[7]));
endmodule
